// Logisim project MIPS.circ as structural Verilog: 5 circuits, main circuit main
module main (
  input  Cin,
  output [4:0] Opcode,
  output ShiftL,
  output ShiftR,
  output Zero,
  output MemWrite,
  output [23:0] Read1_A,
  output [23:0] out_8,
  output [23:0] B,
  output [23:0] MemOutput,
  output RegWrite,
  output [5:0] RS,
  output [22:0] Instruction,
  output [23:0] Read2,
  output [5:0] RT,
  output ALUSrc,
  output MemToReg,
  output Cout,
  output [5:0] RD,
  output RegDst,
  output [2:0] ALUop
);

  wire and_1_out, and_2_out, clock_1_out, control_1_bne, control_1_branch, control_1_j, not_1_out, or_1_out;
  wire [5:0] multiplexer_1_out;
  wire [6:0] bit_extender_4_out;
  wire [9:0] adder_1_out, adder_2_out, bit_extender_1_out, bit_extender_2_out, multiplexer_2_out,
       multiplexer_3_out, register_1_q;
  wire [23:0] alu_1_s, bit_extender_3_out;

  Register #(.width(10)) register_1 (.D(multiplexer_3_out), .clk(clock_1_out), .Q(register_1_q));  // open: en, clr
  ROM #(.addrWidth(10), .dataWidth(23)) rom_1 (.addr(register_1_q), .data(Instruction));
  Adder #(.width(10)) adder_1 (.a(10'h1), .b(register_1_q), .out(adder_1_out));  // open: cin, cout
  Bit_Extender #(.in_width(18), .out_width(10)) bit_extender_1 (.in(Instruction[17:0]), .out(bit_extender_1_out));
  Clock clock_1 (.out(clock_1_out));
  Control control_1 (
    .Opcode(Instruction[22:18]), .RegDst(RegDst), .ALUSrc(ALUSrc), .MemtoReg(MemToReg), .RegWrite(RegWrite),
    .MemWrite(MemWrite), .Branch(control_1_branch), .BNE(control_1_bne), .ALUOp(ALUop), .ShiftL(ShiftL),
    .ShiftR(ShiftR), .J(control_1_j));
  Multiplexer #(.width(6)) multiplexer_1 (
    .in0(Instruction[17:12]), .in1(Instruction[5:0]), .out(multiplexer_1_out), .sel(RegDst));
  assign bit_extender_2_out = {{4{Instruction[5]}}, Instruction[5:0]};  // Bit_Extender bit_extender_2
  Adder #(.width(10)) adder_2 (.a(adder_1_out), .b(bit_extender_2_out), .out(adder_2_out));  // open: cin, cout
  and and_1 (and_1_out, control_1_branch, Zero);
  not not_1 (not_1_out, Zero);
  REGFILE regfile_1 (
    .WD(out_8), .CLK(clock_1_out), .WC(RegWrite), .RD(multiplexer_1_out), .RS(Instruction[11:6]),
    .RT(Instruction[5:0]), .Read1(Read1_A), .Read2(Read2));
  assign bit_extender_3_out = {{18{Instruction[5]}}, Instruction[5:0]};  // Bit_Extender bit_extender_3
  and and_2 (and_2_out, not_1_out, control_1_bne);
  or or_1 (or_1_out, and_1_out, and_2_out);
  Multiplexer #(.width(10)) multiplexer_2 (
    .in0(adder_1_out), .in1(adder_2_out), .out(multiplexer_2_out), .sel(or_1_out));
  Multiplexer #(.width(10)) multiplexer_3 (
    .in0(multiplexer_2_out), .in1(bit_extender_1_out), .out(multiplexer_3_out), .sel(control_1_j));
  Multiplexer #(.width(24)) multiplexer_4 (.in0(Read2), .in1(bit_extender_3_out), .out(B), .sel(ALUSrc));
  ALU alu_1 (
    .Sel(ALUop), .A(Read1_A), .ShiftL(ShiftL), .ShiftR(ShiftR), .B(B), .Cin(Cin), .Cout(Cout), .Zero(Zero),
    .S(alu_1_s));
  RAM #(.addrWidth(7), .dataWidth(24), .enables("line")) ram_1 (
    .addr(bit_extender_4_out), .we(MemWrite), .clk(clock_1_out), .din(Read2), .dout(MemOutput));
  Bit_Extender #(.in_width(24), .out_width(7)) bit_extender_4 (.in(alu_1_s), .out(bit_extender_4_out));
  Multiplexer #(.width(24)) multiplexer_5 (.in0(alu_1_s), .in1(MemOutput), .out(out_8), .sel(MemToReg));

  assign Opcode = Instruction[22:18];
  assign RD = Instruction[17:12];
  assign RS = Instruction[11:6];
  assign RT = Instruction[5:0];

  // Notes on the sheet:
  //   contents of rom_1 (hex, n*v repeats v):
  //   80001 6*0 8001 8001 80001 80001 80001 4*0 440000
endmodule

module REGFILE (
  input  [23:0] WD,
  input  CLK,
  input  WC,
  input  [5:0] RD,
  input  [5:0] RS,
  input  [5:0] RT,
  output [23:0] Read1,
  output [23:0] Read2
);

  wire and_1_out, and_2_out, and_3_out, and_4_out, and_5_out, and_6_out, and_7_out, and_8_out, and_9_out,
       and_10_out, and_11_out, and_12_out, and_13_out, and_14_out, and_15_out, and_16_out, and_17_out,
       and_18_out, and_19_out, and_20_out, and_21_out, and_22_out, and_23_out, and_24_out, and_25_out,
       and_26_out, and_27_out, and_28_out, and_29_out, and_30_out, and_31_out, and_32_out, and_33_out,
       and_34_out, and_35_out, and_36_out, and_37_out, and_38_out, and_39_out, and_40_out, and_41_out,
       and_42_out, and_43_out, and_44_out, and_45_out, and_46_out, and_47_out, and_48_out, and_49_out,
       and_50_out, and_51_out, and_52_out, and_53_out, and_54_out, and_55_out, and_56_out, and_57_out,
       and_58_out, and_59_out, and_60_out, and_61_out, and_62_out, and_63_out, and_64_out, decoder_1_out0,
       decoder_1_out1, decoder_1_out2, decoder_1_out3, decoder_1_out4, decoder_1_out5, decoder_1_out6,
       decoder_1_out7, decoder_1_out8, decoder_1_out9, decoder_1_out10, decoder_1_out11, decoder_1_out12,
       decoder_1_out13, decoder_1_out14, decoder_1_out15, decoder_1_out16, decoder_1_out17, decoder_1_out18,
       decoder_1_out19, decoder_1_out20, decoder_1_out21, decoder_1_out22, decoder_1_out23, decoder_1_out24,
       decoder_1_out25, decoder_1_out26, decoder_1_out27, decoder_1_out28, decoder_1_out29, decoder_1_out30,
       decoder_1_out31, decoder_1_out32, decoder_1_out33, decoder_1_out34, decoder_1_out35, decoder_1_out36,
       decoder_1_out37, decoder_1_out38, decoder_1_out39, decoder_1_out40, decoder_1_out41, decoder_1_out42,
       decoder_1_out43, decoder_1_out44, decoder_1_out45, decoder_1_out46, decoder_1_out47, decoder_1_out48,
       decoder_1_out49, decoder_1_out50, decoder_1_out51, decoder_1_out52, decoder_1_out53, decoder_1_out54,
       decoder_1_out55, decoder_1_out56, decoder_1_out57, decoder_1_out58, decoder_1_out59, decoder_1_out60,
       decoder_1_out61, decoder_1_out62, decoder_1_out63;
  wire [23:0] register_1_q, register_2_q, register_3_q, register_4_q, register_5_q, register_6_q,
       register_7_q, register_8_q, register_9_q, register_10_q, register_11_q, register_12_q, register_13_q,
       register_14_q, register_15_q, register_16_q, register_17_q, register_18_q, register_19_q,
       register_20_q, register_21_q, register_22_q, register_23_q, register_24_q, register_25_q,
       register_26_q, register_27_q, register_28_q, register_29_q, register_30_q, register_31_q,
       register_32_q, register_33_q, register_34_q, register_35_q, register_36_q, register_37_q,
       register_38_q, register_39_q, register_40_q, register_41_q, register_42_q, register_43_q,
       register_44_q, register_45_q, register_46_q, register_47_q, register_48_q, register_49_q,
       register_50_q, register_51_q, register_52_q, register_53_q, register_54_q, register_55_q,
       register_56_q, register_57_q, register_58_q, register_59_q, register_60_q, register_61_q,
       register_62_q, register_63_q, register_64_q;

  Decoder #(.select(6)) decoder_1 (
    .out0(decoder_1_out0), .out1(decoder_1_out1), .out2(decoder_1_out2), .out3(decoder_1_out3),
    .out4(decoder_1_out4), .out5(decoder_1_out5), .out6(decoder_1_out6), .out7(decoder_1_out7),
    .out8(decoder_1_out8), .out9(decoder_1_out9), .out10(decoder_1_out10), .out11(decoder_1_out11),
    .out12(decoder_1_out12), .out13(decoder_1_out13), .out14(decoder_1_out14), .out15(decoder_1_out15),
    .out16(decoder_1_out16), .out17(decoder_1_out17), .out18(decoder_1_out18), .out19(decoder_1_out19),
    .out20(decoder_1_out20), .out21(decoder_1_out21), .out22(decoder_1_out22), .out23(decoder_1_out23),
    .out24(decoder_1_out24), .out25(decoder_1_out25), .out26(decoder_1_out26), .out27(decoder_1_out27),
    .out28(decoder_1_out28), .out29(decoder_1_out29), .out30(decoder_1_out30), .out31(decoder_1_out31),
    .out32(decoder_1_out32), .out33(decoder_1_out33), .out34(decoder_1_out34), .out35(decoder_1_out35),
    .out36(decoder_1_out36), .out37(decoder_1_out37), .out38(decoder_1_out38), .out39(decoder_1_out39),
    .out40(decoder_1_out40), .out41(decoder_1_out41), .out42(decoder_1_out42), .out43(decoder_1_out43),
    .out44(decoder_1_out44), .out45(decoder_1_out45), .out46(decoder_1_out46), .out47(decoder_1_out47),
    .out48(decoder_1_out48), .out49(decoder_1_out49), .out50(decoder_1_out50), .out51(decoder_1_out51),
    .out52(decoder_1_out52), .out53(decoder_1_out53), .out54(decoder_1_out54), .out55(decoder_1_out55),
    .out56(decoder_1_out56), .out57(decoder_1_out57), .out58(decoder_1_out58), .out59(decoder_1_out59),
    .out60(decoder_1_out60), .out61(decoder_1_out61), .out62(decoder_1_out62), .out63(decoder_1_out63),
    .sel(RD));  // open: en
  and and_1 (and_1_out, decoder_1_out0, WC);
  and and_2 (and_2_out, decoder_1_out1, WC);
  and and_3 (and_3_out, decoder_1_out2, WC);
  and and_4 (and_4_out, decoder_1_out3, WC);
  and and_5 (and_5_out, decoder_1_out4, WC);
  and and_6 (and_6_out, decoder_1_out5, WC);
  and and_7 (and_7_out, decoder_1_out6, WC);
  and and_8 (and_8_out, decoder_1_out7, WC);
  and and_9 (and_9_out, decoder_1_out32, WC);
  and and_10 (and_10_out, decoder_1_out33, WC);
  and and_11 (and_11_out, decoder_1_out34, WC);
  and and_12 (and_12_out, decoder_1_out35, WC);
  and and_13 (and_13_out, decoder_1_out36, WC);
  and and_14 (and_14_out, decoder_1_out37, WC);
  and and_15 (and_15_out, decoder_1_out38, WC);
  and and_16 (and_16_out, decoder_1_out39, WC);
  Register #(.width(24)) register_1 (.D(WD), .en(and_1_out), .clk(CLK), .Q(register_1_q));  // open: clr
  Register #(.width(24)) register_2 (.D(WD), .en(and_2_out), .clk(CLK), .Q(register_2_q));  // open: clr
  Register #(.width(24)) register_3 (.D(WD), .en(and_3_out), .clk(CLK), .Q(register_3_q));  // open: clr
  Register #(.width(24)) register_4 (.D(WD), .en(and_4_out), .clk(CLK), .Q(register_4_q));  // open: clr
  Register #(.width(24)) register_5 (.D(WD), .en(and_5_out), .clk(CLK), .Q(register_5_q));  // open: clr
  Register #(.width(24)) register_6 (.D(WD), .en(and_6_out), .clk(CLK), .Q(register_6_q));  // open: clr
  Register #(.width(24)) register_7 (.D(WD), .en(and_7_out), .clk(CLK), .Q(register_7_q));  // open: clr
  Register #(.width(24)) register_8 (.D(WD), .en(and_8_out), .clk(CLK), .Q(register_8_q));  // open: clr
  Register #(.width(24)) register_9 (.D(WD), .en(and_9_out), .clk(CLK), .Q(register_9_q));  // open: clr
  Register #(.width(24)) register_10 (.D(WD), .en(and_10_out), .clk(CLK), .Q(register_10_q));  // open: clr
  Register #(.width(24)) register_11 (.D(WD), .en(and_11_out), .clk(CLK), .Q(register_11_q));  // open: clr
  Register #(.width(24)) register_12 (.D(WD), .en(and_12_out), .clk(CLK), .Q(register_12_q));  // open: clr
  Register #(.width(24)) register_13 (.D(WD), .en(and_13_out), .clk(CLK), .Q(register_13_q));  // open: clr
  Register #(.width(24)) register_14 (.D(WD), .en(and_14_out), .clk(CLK), .Q(register_14_q));  // open: clr
  Register #(.width(24)) register_15 (.D(WD), .en(and_15_out), .clk(CLK), .Q(register_15_q));  // open: clr
  Register #(.width(24)) register_16 (.D(WD), .en(and_16_out), .clk(CLK), .Q(register_16_q));  // open: clr
  Register #(.width(24)) register_17 (.D(WD), .en(and_17_out), .clk(CLK), .Q(register_17_q));  // open: clr
  and and_17 (and_17_out, decoder_1_out8, WC);
  Register #(.width(24)) register_18 (.D(WD), .en(and_18_out), .clk(CLK), .Q(register_18_q));  // open: clr
  and and_18 (and_18_out, decoder_1_out9, WC);
  Register #(.width(24)) register_19 (.D(WD), .en(and_19_out), .clk(CLK), .Q(register_19_q));  // open: clr
  and and_19 (and_19_out, decoder_1_out10, WC);
  Register #(.width(24)) register_20 (.D(WD), .en(and_20_out), .clk(CLK), .Q(register_20_q));  // open: clr
  and and_20 (and_20_out, decoder_1_out11, WC);
  Register #(.width(24)) register_21 (.D(WD), .en(and_21_out), .clk(CLK), .Q(register_21_q));  // open: clr
  and and_21 (and_21_out, decoder_1_out12, WC);
  Register #(.width(24)) register_22 (.D(WD), .en(and_22_out), .clk(CLK), .Q(register_22_q));  // open: clr
  and and_22 (and_22_out, decoder_1_out13, WC);
  Register #(.width(24)) register_23 (.D(WD), .en(and_23_out), .clk(CLK), .Q(register_23_q));  // open: clr
  and and_23 (and_23_out, decoder_1_out14, WC);
  Register #(.width(24)) register_24 (.D(WD), .en(and_24_out), .clk(CLK), .Q(register_24_q));  // open: clr
  and and_24 (and_24_out, decoder_1_out15, WC);
  Register #(.width(24)) register_25 (.D(WD), .en(and_25_out), .clk(CLK), .Q(register_25_q));  // open: clr
  and and_25 (and_25_out, decoder_1_out40, WC);
  Register #(.width(24)) register_26 (.D(WD), .en(and_26_out), .clk(CLK), .Q(register_26_q));  // open: clr
  and and_26 (and_26_out, decoder_1_out41, WC);
  Register #(.width(24)) register_27 (.D(WD), .en(and_27_out), .clk(CLK), .Q(register_27_q));  // open: clr
  and and_27 (and_27_out, decoder_1_out42, WC);
  Register #(.width(24)) register_28 (.D(WD), .en(and_28_out), .clk(CLK), .Q(register_28_q));  // open: clr
  and and_28 (and_28_out, decoder_1_out43, WC);
  Register #(.width(24)) register_29 (.D(WD), .en(and_29_out), .clk(CLK), .Q(register_29_q));  // open: clr
  and and_29 (and_29_out, decoder_1_out44, WC);
  Register #(.width(24)) register_30 (.D(WD), .en(and_30_out), .clk(CLK), .Q(register_30_q));  // open: clr
  and and_30 (and_30_out, decoder_1_out45, WC);
  Register #(.width(24)) register_31 (.D(WD), .en(and_31_out), .clk(CLK), .Q(register_31_q));  // open: clr
  and and_31 (and_31_out, decoder_1_out46, WC);
  Register #(.width(24)) register_32 (.D(WD), .en(and_32_out), .clk(CLK), .Q(register_32_q));  // open: clr
  and and_32 (and_32_out, decoder_1_out47, WC);
  and and_33 (and_33_out, decoder_1_out16, WC);
  and and_34 (and_34_out, decoder_1_out17, WC);
  and and_35 (and_35_out, decoder_1_out18, WC);
  and and_36 (and_36_out, decoder_1_out19, WC);
  and and_37 (and_37_out, decoder_1_out20, WC);
  and and_38 (and_38_out, decoder_1_out21, WC);
  and and_39 (and_39_out, decoder_1_out22, WC);
  and and_40 (and_40_out, decoder_1_out23, WC);
  and and_41 (and_41_out, decoder_1_out48, WC);
  and and_42 (and_42_out, decoder_1_out49, WC);
  and and_43 (and_43_out, decoder_1_out50, WC);
  and and_44 (and_44_out, decoder_1_out51, WC);
  and and_45 (and_45_out, decoder_1_out52, WC);
  and and_46 (and_46_out, decoder_1_out53, WC);
  and and_47 (and_47_out, decoder_1_out54, WC);
  and and_48 (and_48_out, decoder_1_out55, WC);
  Register #(.width(24)) register_33 (.D(WD), .en(and_33_out), .clk(CLK), .Q(register_33_q));  // open: clr
  Register #(.width(24)) register_34 (.D(WD), .en(and_34_out), .clk(CLK), .Q(register_34_q));  // open: clr
  Register #(.width(24)) register_35 (.D(WD), .en(and_35_out), .clk(CLK), .Q(register_35_q));  // open: clr
  Register #(.width(24)) register_36 (.D(WD), .en(and_36_out), .clk(CLK), .Q(register_36_q));  // open: clr
  Register #(.width(24)) register_37 (.D(WD), .en(and_37_out), .clk(CLK), .Q(register_37_q));  // open: clr
  Register #(.width(24)) register_38 (.D(WD), .en(and_38_out), .clk(CLK), .Q(register_38_q));  // open: clr
  Register #(.width(24)) register_39 (.D(WD), .en(and_39_out), .clk(CLK), .Q(register_39_q));  // open: clr
  Register #(.width(24)) register_40 (.D(WD), .en(and_40_out), .clk(CLK), .Q(register_40_q));  // open: clr
  Register #(.width(24)) register_41 (.D(WD), .en(and_41_out), .clk(CLK), .Q(register_41_q));  // open: clr
  Register #(.width(24)) register_42 (.D(WD), .en(and_42_out), .clk(CLK), .Q(register_42_q));  // open: clr
  Register #(.width(24)) register_43 (.D(WD), .en(and_43_out), .clk(CLK), .Q(register_43_q));  // open: clr
  Register #(.width(24)) register_44 (.D(WD), .en(and_44_out), .clk(CLK), .Q(register_44_q));  // open: clr
  Register #(.width(24)) register_45 (.D(WD), .en(and_45_out), .clk(CLK), .Q(register_45_q));  // open: clr
  Register #(.width(24)) register_46 (.D(WD), .en(and_46_out), .clk(CLK), .Q(register_46_q));  // open: clr
  Register #(.width(24)) register_47 (.D(WD), .en(and_47_out), .clk(CLK), .Q(register_47_q));  // open: clr
  Register #(.width(24)) register_48 (.D(WD), .en(and_48_out), .clk(CLK), .Q(register_48_q));  // open: clr
  and and_49 (and_49_out, decoder_1_out24, WC);
  and and_50 (and_50_out, decoder_1_out25, WC);
  and and_51 (and_51_out, decoder_1_out26, WC);
  and and_52 (and_52_out, decoder_1_out27, WC);
  and and_53 (and_53_out, decoder_1_out28, WC);
  and and_54 (and_54_out, decoder_1_out29, WC);
  and and_55 (and_55_out, decoder_1_out30, WC);
  and and_56 (and_56_out, decoder_1_out31, WC);
  and and_57 (and_57_out, decoder_1_out56, WC);
  and and_58 (and_58_out, decoder_1_out57, WC);
  and and_59 (and_59_out, decoder_1_out58, WC);
  and and_60 (and_60_out, decoder_1_out59, WC);
  and and_61 (and_61_out, decoder_1_out60, WC);
  and and_62 (and_62_out, decoder_1_out61, WC);
  and and_63 (and_63_out, decoder_1_out62, WC);
  and and_64 (and_64_out, decoder_1_out63, WC);
  Register #(.width(24)) register_49 (.D(WD), .en(and_49_out), .clk(CLK), .Q(register_49_q));  // open: clr
  Register #(.width(24)) register_50 (.D(WD), .en(and_50_out), .clk(CLK), .Q(register_50_q));  // open: clr
  Register #(.width(24)) register_51 (.D(WD), .en(and_51_out), .clk(CLK), .Q(register_51_q));  // open: clr
  Register #(.width(24)) register_52 (.D(WD), .en(and_52_out), .clk(CLK), .Q(register_52_q));  // open: clr
  Register #(.width(24)) register_53 (.D(WD), .en(and_53_out), .clk(CLK), .Q(register_53_q));  // open: clr
  Register #(.width(24)) register_54 (.D(WD), .en(and_54_out), .clk(CLK), .Q(register_54_q));  // open: clr
  Register #(.width(24)) register_55 (.D(WD), .en(and_55_out), .clk(CLK), .Q(register_55_q));  // open: clr
  Register #(.width(24)) register_56 (.D(WD), .en(and_56_out), .clk(CLK), .Q(register_56_q));  // open: clr
  Register #(.width(24)) register_57 (.D(WD), .en(and_57_out), .clk(CLK), .Q(register_57_q));  // open: clr
  Register #(.width(24)) register_58 (.D(WD), .en(and_58_out), .clk(CLK), .Q(register_58_q));  // open: clr
  Register #(.width(24)) register_59 (.D(WD), .en(and_59_out), .clk(CLK), .Q(register_59_q));  // open: clr
  Register #(.width(24)) register_60 (.D(WD), .en(and_60_out), .clk(CLK), .Q(register_60_q));  // open: clr
  Register #(.width(24)) register_61 (.D(WD), .en(and_61_out), .clk(CLK), .Q(register_61_q));  // open: clr
  Register #(.width(24)) register_62 (.D(WD), .en(and_62_out), .clk(CLK), .Q(register_62_q));  // open: clr
  Register #(.width(24)) register_63 (.D(WD), .en(and_63_out), .clk(CLK), .Q(register_63_q));  // open: clr
  Register #(.width(24)) register_64 (.D(WD), .en(and_64_out), .clk(CLK), .Q(register_64_q));  // open: clr
  Multiplexer #(.select(6), .width(24)) multiplexer_1 (
    .in0(register_1_q), .in1(register_2_q), .in2(register_3_q), .in3(register_4_q), .in4(register_5_q),
    .in5(register_6_q), .in6(register_7_q), .in7(register_8_q), .in8(register_17_q), .in9(register_18_q),
    .in10(register_19_q), .in11(register_20_q), .in12(register_21_q), .in13(register_22_q),
    .in14(register_23_q), .in15(register_24_q), .in16(register_33_q), .in17(register_34_q),
    .in18(register_35_q), .in19(register_36_q), .in20(register_37_q), .in21(register_38_q),
    .in22(register_39_q), .in23(register_40_q), .in24(register_49_q), .in25(register_50_q),
    .in26(register_51_q), .in27(register_52_q), .in28(register_53_q), .in29(register_54_q),
    .in30(register_55_q), .in31(register_56_q), .in32(register_9_q), .in33(register_10_q),
    .in34(register_11_q), .in35(register_12_q), .in36(register_13_q), .in37(register_14_q),
    .in38(register_15_q), .in39(register_16_q), .in40(register_25_q), .in41(register_26_q),
    .in42(register_27_q), .in43(register_28_q), .in44(register_29_q), .in45(register_30_q),
    .in46(register_31_q), .in47(register_32_q), .in48(register_41_q), .in49(register_42_q),
    .in50(register_43_q), .in51(register_44_q), .in52(register_45_q), .in53(register_46_q),
    .in54(register_47_q), .in55(register_48_q), .in56(register_57_q), .in57(register_58_q),
    .in58(register_59_q), .in59(register_60_q), .in60(register_61_q), .in61(register_62_q),
    .in62(register_63_q), .in63(register_64_q), .out(Read1), .sel(RS));
  Multiplexer #(.select(6), .width(24)) multiplexer_2 (
    .in0(register_1_q), .in1(register_2_q), .in2(register_3_q), .in3(register_4_q), .in4(register_5_q),
    .in5(register_6_q), .in6(register_7_q), .in7(register_8_q), .in8(register_17_q), .in9(register_18_q),
    .in10(register_19_q), .in11(register_20_q), .in12(register_21_q), .in13(register_22_q),
    .in14(register_23_q), .in15(register_24_q), .in16(register_33_q), .in17(register_34_q),
    .in18(register_35_q), .in19(register_36_q), .in20(register_37_q), .in21(register_38_q),
    .in22(register_39_q), .in23(register_40_q), .in24(register_49_q), .in25(register_50_q),
    .in26(register_51_q), .in27(register_52_q), .in28(register_53_q), .in29(register_54_q),
    .in30(register_55_q), .in31(register_56_q), .in32(register_9_q), .in33(register_10_q),
    .in34(register_11_q), .in35(register_12_q), .in36(register_13_q), .in37(register_14_q),
    .in38(register_15_q), .in39(register_16_q), .in40(register_25_q), .in41(register_26_q),
    .in42(register_27_q), .in43(register_28_q), .in44(register_29_q), .in45(register_30_q),
    .in46(register_31_q), .in47(register_32_q), .in48(register_41_q), .in49(register_42_q),
    .in50(register_43_q), .in51(register_44_q), .in52(register_45_q), .in53(register_46_q),
    .in54(register_47_q), .in55(register_48_q), .in56(register_57_q), .in57(register_58_q),
    .in58(register_59_q), .in59(register_60_q), .in60(register_61_q), .in61(register_62_q),
    .in62(register_63_q), .in63(register_64_q), .out(Read2), .sel(RT));
endmodule

module OneBitALU (
  input  A,
  input  B,
  input  Cin,
  input  [2:0] Sel,
  output Y,
  output Cout
);

  wire adder_1_out, and_1_out, nand_1_out, nor_1_out, not_1_out, or_1_out, xor_1_out, xor_2_out;

  xor xor_1 (xor_1_out, B, Sel[0]);
  Adder #(.width(1)) adder_1 (.a(A), .b(xor_1_out), .out(adder_1_out), .cin(Cin), .cout(Cout));
  and and_1 (and_1_out, A, B);
  or or_1 (or_1_out, A, B);
  xor xor_2 (xor_2_out, A, B);
  nor nor_1 (nor_1_out, A, B);
  not not_1 (not_1_out, A);
  nand nand_1 (nand_1_out, A, B);
  Multiplexer #(.select(3)) multiplexer_1 (
    .in0(and_1_out), .in1(or_1_out), .in2(adder_1_out), .in3(adder_1_out), .in4(xor_2_out), .in5(nor_1_out),
    .in6(not_1_out), .in7(nand_1_out), .out(Y), .sel(Sel));
endmodule

module ALU (
  input  [23:0] B,
  input  Cin,
  input  [23:0] A,
  input  ShiftL,
  input  ShiftR,
  input  [2:0] Sel,
  output [23:0] S,
  output Zero,
  output Cout
);

  wire onebitalu_1_cout, onebitalu_2_cout, onebitalu_3_cout, onebitalu_4_cout, onebitalu_5_cout,
       onebitalu_6_cout, onebitalu_7_cout, onebitalu_8_cout, onebitalu_9_cout, onebitalu_10_cout,
       onebitalu_11_cout, onebitalu_12_cout, onebitalu_13_cout, onebitalu_14_cout, onebitalu_15_cout,
       onebitalu_16_cout, onebitalu_17_cout, onebitalu_18_cout, onebitalu_19_cout, onebitalu_20_cout,
       onebitalu_21_cout, onebitalu_22_cout, onebitalu_23_cout;
  wire [4:0] bit_extender_1_out;
  wire [23:0] multiplexer_1_out, onebitalu_1_y, shifter_1_out, shifter_2_out;

  OneBitALU onebitalu_1 (.A(A[0]), .B(B[0]), .Cin(Cin), .Sel(Sel), .Y(onebitalu_1_y[0]), .Cout(onebitalu_1_cout));
  OneBitALU onebitalu_2 (
    .A(A[1]), .B(B[1]), .Cin(onebitalu_1_cout), .Sel(Sel), .Y(onebitalu_1_y[1]), .Cout(onebitalu_2_cout));
  OneBitALU onebitalu_3 (
    .A(A[2]), .B(B[2]), .Cin(onebitalu_2_cout), .Sel(Sel), .Y(onebitalu_1_y[2]), .Cout(onebitalu_3_cout));
  OneBitALU onebitalu_4 (
    .A(A[3]), .B(B[3]), .Cin(onebitalu_3_cout), .Sel(Sel), .Y(onebitalu_1_y[3]), .Cout(onebitalu_4_cout));
  OneBitALU onebitalu_5 (
    .A(A[4]), .B(B[4]), .Cin(onebitalu_4_cout), .Sel(Sel), .Y(onebitalu_1_y[4]), .Cout(onebitalu_5_cout));
  OneBitALU onebitalu_6 (
    .A(A[5]), .B(B[5]), .Cin(onebitalu_5_cout), .Sel(Sel), .Y(onebitalu_1_y[5]), .Cout(onebitalu_6_cout));
  OneBitALU onebitalu_7 (
    .A(A[6]), .B(B[6]), .Cin(onebitalu_6_cout), .Sel(Sel), .Y(onebitalu_1_y[6]), .Cout(onebitalu_7_cout));
  OneBitALU onebitalu_8 (
    .A(A[7]), .B(B[7]), .Cin(onebitalu_7_cout), .Sel(Sel), .Y(onebitalu_1_y[7]), .Cout(onebitalu_8_cout));
  OneBitALU onebitalu_9 (
    .A(A[8]), .B(B[8]), .Cin(onebitalu_8_cout), .Sel(Sel), .Y(onebitalu_1_y[8]), .Cout(onebitalu_9_cout));
  OneBitALU onebitalu_10 (
    .A(A[9]), .B(B[9]), .Cin(onebitalu_9_cout), .Sel(Sel), .Y(onebitalu_1_y[9]), .Cout(onebitalu_10_cout));
  OneBitALU onebitalu_11 (
    .A(A[10]), .B(B[10]), .Cin(onebitalu_10_cout), .Sel(Sel), .Y(onebitalu_1_y[10]), .Cout(onebitalu_11_cout));
  OneBitALU onebitalu_12 (
    .A(A[11]), .B(B[11]), .Cin(onebitalu_11_cout), .Sel(Sel), .Y(onebitalu_1_y[11]), .Cout(onebitalu_12_cout));
  OneBitALU onebitalu_13 (
    .A(A[12]), .B(B[12]), .Cin(onebitalu_12_cout), .Sel(Sel), .Y(onebitalu_1_y[12]), .Cout(onebitalu_13_cout));
  OneBitALU onebitalu_14 (
    .A(A[13]), .B(B[13]), .Cin(onebitalu_13_cout), .Sel(Sel), .Y(onebitalu_1_y[13]), .Cout(onebitalu_14_cout));
  OneBitALU onebitalu_15 (
    .A(A[14]), .B(B[14]), .Cin(onebitalu_14_cout), .Sel(Sel), .Y(onebitalu_1_y[14]), .Cout(onebitalu_15_cout));
  OneBitALU onebitalu_16 (
    .A(A[15]), .B(B[15]), .Cin(onebitalu_15_cout), .Sel(Sel), .Y(onebitalu_1_y[15]), .Cout(onebitalu_16_cout));
  OneBitALU onebitalu_17 (
    .A(A[16]), .B(B[16]), .Cin(onebitalu_16_cout), .Sel(Sel), .Y(onebitalu_1_y[16]), .Cout(onebitalu_17_cout));
  OneBitALU onebitalu_18 (
    .A(A[17]), .B(B[17]), .Cin(onebitalu_17_cout), .Sel(Sel), .Y(onebitalu_1_y[17]), .Cout(onebitalu_18_cout));
  OneBitALU onebitalu_19 (
    .A(A[18]), .B(B[18]), .Cin(onebitalu_18_cout), .Sel(Sel), .Y(onebitalu_1_y[18]), .Cout(onebitalu_19_cout));
  OneBitALU onebitalu_20 (
    .A(A[19]), .B(B[19]), .Cin(onebitalu_19_cout), .Sel(Sel), .Y(onebitalu_1_y[19]), .Cout(onebitalu_20_cout));
  OneBitALU onebitalu_21 (
    .A(A[20]), .B(B[20]), .Cin(onebitalu_20_cout), .Sel(Sel), .Y(onebitalu_1_y[20]), .Cout(onebitalu_21_cout));
  OneBitALU onebitalu_22 (
    .A(A[21]), .B(B[21]), .Cin(onebitalu_21_cout), .Sel(Sel), .Y(onebitalu_1_y[21]), .Cout(onebitalu_22_cout));
  OneBitALU onebitalu_23 (
    .A(A[22]), .B(B[22]), .Cin(onebitalu_22_cout), .Sel(Sel), .Y(onebitalu_1_y[22]), .Cout(onebitalu_23_cout));
  OneBitALU onebitalu_24 (.A(A[23]), .B(B[23]), .Cin(onebitalu_23_cout), .Sel(Sel), .Y(onebitalu_1_y[23]), .Cout(Cout));
  Bit_Extender #(.in_width(24), .out_width(5)) bit_extender_1 (.in(B), .out(bit_extender_1_out));
  nor nor_1 (Zero, onebitalu_1_y[0], onebitalu_1_y[1], onebitalu_1_y[2], onebitalu_1_y[3], onebitalu_1_y[4], onebitalu_1_y[5], onebitalu_1_y[6], onebitalu_1_y[7], onebitalu_1_y[8], onebitalu_1_y[9], onebitalu_1_y[10], onebitalu_1_y[11], onebitalu_1_y[12], onebitalu_1_y[13], onebitalu_1_y[14], onebitalu_1_y[15], onebitalu_1_y[16], onebitalu_1_y[17], onebitalu_1_y[18], onebitalu_1_y[19], onebitalu_1_y[20], onebitalu_1_y[21], onebitalu_1_y[22], onebitalu_1_y[23]);
  Shifter #(.width(24)) shifter_1 (.in(A), .\dist (bit_extender_1_out), .out(shifter_1_out));
  Multiplexer #(.width(24)) multiplexer_1 (
    .in0(onebitalu_1_y), .in1(shifter_1_out), .out(multiplexer_1_out), .sel(ShiftL));
  Shifter #(.shift("lr"), .width(24)) shifter_2 (.in(A), .\dist (bit_extender_1_out), .out(shifter_2_out));
  Multiplexer #(.width(24)) multiplexer_2 (.in0(multiplexer_1_out), .in1(shifter_2_out), .out(S), .sel(ShiftR));
endmodule

module Control (
  input  [4:0] Opcode,
  output RegDst,
  output ALUSrc,
  output MemtoReg,
  output RegWrite,
  output MemWrite,
  output Branch,
  output BNE,
  output [2:0] ALUOp,
  output ShiftL,
  output ShiftR,
  output J
);

  wire and_1_out, and_2_out, and_3_out, and_4_out, and_5_out, and_6_out, and_7_out, and_8_out, and_10_out,
       and_11_out, and_12_out, and_13_out, and_15_out, and_16_out, and_18_out, and_19_out, and_20_out,
       and_21_out, and_22_out, and_23_out, and_24_out, and_25_out, and_26_out, and_27_out, and_28_out,
       not_1_out, not_2_out, not_3_out, not_4_out, not_5_out;

  not not_1 (not_1_out, Opcode[4]);
  not not_2 (not_2_out, Opcode[3]);
  not not_3 (not_3_out, Opcode[2]);
  not not_4 (not_4_out, Opcode[1]);
  not not_5 (not_5_out, Opcode[0]);
  and and_1 (and_1_out, not_1_out, not_2_out, Opcode[0]);
  and and_2 (and_2_out, not_1_out, not_3_out, not_4_out, Opcode[0]);
  or or_1 (RegDst, and_1_out, and_2_out, and_3_out);
  and and_3 (and_3_out, not_1_out, Opcode[3], Opcode[1], not_5_out);
  and and_4 (and_4_out, not_1_out, not_2_out, Opcode[1], not_5_out);
  and and_5 (and_5_out, not_1_out, Opcode[2], not_5_out);
  and and_6 (and_6_out, not_1_out, Opcode[3], not_4_out, not_5_out);
  and and_7 (and_7_out, not_1_out, Opcode[3], not_3_out, Opcode[1], Opcode[0]);
  and and_8 (and_8_out, not_1_out, Opcode[3], Opcode[2], not_4_out);
  and and_9 (MemtoReg, not_1_out, Opcode[3], Opcode[2], Opcode[0]);
  and and_10 (and_10_out, not_1_out, not_2_out, Opcode[1]);
  and and_11 (and_11_out, not_1_out, Opcode[3], not_3_out);
  and and_12 (and_12_out, not_1_out, not_4_out, Opcode[0]);
  and and_13 (and_13_out, not_1_out, Opcode[2], not_4_out);
  and and_14 (MemWrite, not_1_out, Opcode[3], Opcode[2], Opcode[1], not_5_out);
  and and_15 (and_15_out, Opcode[4], not_2_out, not_3_out, not_4_out);
  or or_2 (Branch, and_15_out, and_16_out);
  and and_16 (and_16_out, not_1_out, Opcode[3], Opcode[2], Opcode[1], Opcode[0]);
  and and_17 (BNE, Opcode[4], not_2_out, not_3_out, not_4_out);
  and and_18 (and_18_out, not_1_out, Opcode[3], not_3_out, Opcode[0]);
  or or_3 (ALUOp[2], and_18_out, and_19_out);
  and and_19 (and_19_out, not_1_out, Opcode[3], not_3_out, Opcode[1]);
  and and_20 (and_20_out, Opcode[4], not_2_out, not_3_out, not_4_out);
  and and_21 (and_21_out, not_1_out, not_3_out, Opcode[1]);
  and and_22 (and_22_out, not_1_out, Opcode[2], not_4_out, not_5_out);
  and and_23 (and_23_out, not_1_out, Opcode[3], Opcode[2]);
  and and_24 (and_24_out, not_2_out, not_3_out, not_4_out, Opcode[0]);
  and and_25 (and_25_out, Opcode[4], not_2_out, not_3_out, not_4_out);
  and and_26 (and_26_out, not_1_out, Opcode[1], Opcode[0]);
  and and_27 (and_27_out, not_1_out, Opcode[2], not_4_out, not_5_out);
  and and_28 (and_28_out, not_1_out, Opcode[3], not_3_out, not_4_out);
  and and_29 (ShiftL, not_1_out, Opcode[3], not_3_out, Opcode[1], Opcode[0]);
  and and_30 (ShiftR, not_1_out, Opcode[3], Opcode[2], not_4_out, not_5_out);
  and and_31 (J, Opcode[4], not_2_out, not_3_out, not_4_out, Opcode[0]);
  or or_4 (ALUSrc, and_4_out, and_5_out, and_6_out, and_7_out, and_8_out);
  or or_5 (RegWrite, and_10_out, and_11_out, and_12_out, and_13_out);
  or or_6 (ALUOp[1], and_20_out, and_21_out, and_22_out, and_23_out, and_24_out);
  or or_7 (ALUOp[0], and_25_out, and_26_out, and_27_out, and_28_out);
endmodule
